# Fritzing sketch Untitled Sketch (saved by Fritzing 0.9.3b)

parts:
  U3 = ESP8266 NodeMCU LoLin module
  DHT1 = DHT11 Humitidy and Temperature Sensor
  DS1 = DS18B20 1-Wire Temperature Sensor Probe
  Capacitive_Soil_Moisture_Sensor1 = DFRobot Capacitive Soil Moisture Sensor V1.0 [part_number=SEN0193]
  AMS1 = AMS1777 5V regulator module
  BAT1 = Battery Holders [package=lipo-1100mAh]

nets:
  N1: U3.D2, DS1.DQ
  N2: U3.D4, DHT1.DATA
  GND: U3.GND, Capacitive_Soil_Moisture_Sensor1.GND
  N3: U3.Vin, AMS1.VOUT+
  N4: U3.VU, DHT1.GND
  N5: U3.A0, Capacitive_Soil_Moisture_Sensor1.A
  N6: DHT1.VDD, AMS1.GND-_(output)
  N7: AMS1.VIN+, BAT1.+

custom parts:
  ESP8266 NodeMCU LoLin module: ESP8266 based NodeMCU
  DHT11 Humitidy and Temperature Sensor: DHT11 Humidity and Temperature Sensor
  DFRobot Capacitive Soil Moisture Sensor V1.0: DFRobot Capacitive Soil Moisture Sensor V1.0 This product measures soil moisture levels by capacitive sensing, rather than resistive sensing like other types of moisture sensor. It is made of a corrosion resistant material giving it a long service life. Insert it into soil and impress your friends with the real-time soil moisture data! The product includes an on-board voltage regulator which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
  AMS1777 5V regulator module: AMS1777 5V regulator module source : https://github.com/ShenTengTu/fritzing_parts/tree/master/voltage%20regulator/AMS1117_5V_regulator_module
